// Logisim project 02.circ as structural Verilog: 1 circuit, main circuit main
module main (
  input  in_1,
  input  in_2,
  input  in_3,
  output out_4,
  output out_5,
  output out_6
);

  wire undriven;

  and and_1 (out_4, in_1, in_2);
  or or_1 (out_5, in_1, in_2);
  Multiplexer multiplexer_1 (.in0(out_4), .in1(out_5), .out(out_6), .sel(undriven));  // open: en
endmodule
