// Logisim project Q0301.circ as structural Verilog: 1 circuit, main circuit main
module main (
  input  in_1,
  input  in_2,
  output out_3
);

  wire nand_1_out, nand_2_out, nor_1_out;

  nor nor_1 (nor_1_out, in_1, in_1);
  nand nand_1 (nand_1_out, nor_1_out, in_2);
  nand nand_2 (nand_2_out, nor_1_out, in_2);
  nand nand_3 (out_3, nand_1_out, nand_2_out, nand_2_out);
endmodule
