// Logisim project Q0302.circ as structural Verilog: 1 circuit, main circuit main
module main (
  input  in_1,
  input  a,
  input  in_3,
  output out_4
);

  wire multiplexer_1_out, multiplexer_2_out, not_1_out, not_2_out, not_3_out;

  not not_1 (not_1_out, in_1);
  not not_2 (not_2_out, in_1);
  Multiplexer #(.enable("false")) multiplexer_1 (.in0(in_1), .in1(not_1_out), .out(multiplexer_1_out), .sel(in_3));
  Multiplexer #(.enable("false")) multiplexer_2 (.in0(not_2_out), .in1(in_1), .out(multiplexer_2_out), .sel(not_3_out));
  not not_3 (not_3_out, in_3);
  Multiplexer #(.enable("false")) multiplexer_3 (
    .in0(multiplexer_1_out), .in1(multiplexer_2_out), .out(out_4), .sel(a));
endmodule
